# Fritzing sketch ELECTRIC SCHE (saved by Fritzing 1.0.2b)
breadboards: 1

parts:
  Part1 = Adafruit Feather HUZZAH ESP8266 [part_number="Adafruit #2821"]
  Part2 = Adafruit TSL2591 High Dynamic Range Digital Light Sensor [part_number="Adafruit #1980"]
  LED1 = LED - 5mm [color="Red (633nm)" current=0.030A package="5 mm [THT]"]
  ZS-042_RTC1 = ZS-042 RTC Module
  BAT1 = Battery Holders [package=battery-aa-panel]

nets:
  N1: Part1.GPIO13/MOSI, LED1.anode
  GND: Part1.GND, Part2.GND, LED1.cathode, BAT1.-
  N2: Part1.VBAT, Part2.3.3V, BAT1.+
  N3: Part1.GPIO5/SCL, ZS-042_RTC1.SCL
  N4: Part1.GPIO4/SDA, ZS-042_RTC1.SDA

custom parts:
  Adafruit Feather HUZZAH ESP8266: his is the Adafruit Feather HUZZAH ESP8266 - our take on an 'all-in-one' ESP8266 WiFi development board with built in USB and battery charging. Its an ESP8266 WiFi module with all the extras you need, ready to rock! We have other boards in the Feather family, check'em out here. At the Feather HUZZAH's heart is an ESP8266 WiFi microcontroller clocked at 80 MHz and at 3.3V logic. This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
  Adafruit TSL2591 High Dynamic Range Digital Light Sensor: When the future is dazzlingly-bright, this ultra-high-range luminosity sensor will help you measure it. The TSL2591 luminosity sensor is an advanced digital light sensor, ideal for use in a wide range of light situations. Compared to low cost CdS cells, this sensor is more precise, allowing for exact lux calculations and can be configured for different gain/timing ranges to detect light ranges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
